// Logisim project CPU-1-Logisim.circ as structural Verilog: 1 circuit, main circuit main
module main (
  output SKIP,
  output HALT
);

  wire clock_1_out, comparator_1_eq, controlled_buffer_14_out, demultiplexer_1_out1, demultiplexer_1_out2,
       demultiplexer_1_out3, demultiplexer_1_out4, demultiplexer_1_out5, demultiplexer_1_out6,
       demultiplexer_1_out7, demultiplexer_1_out9, demultiplexer_1_out10, demultiplexer_1_out11,
       demultiplexer_1_out12, demultiplexer_1_out13, demultiplexer_1_out14, demultiplexer_1_out15, GO_out,
       not_1_out, not_2_out, not_3_out, not_5_out, or_1_out, or_3_out, or_4_out, pull_resistor_1_node,
       pull_resistor_2_node, pull_resistor_6_node, RESET_out;
  wire [3:0] controlled_buffer_4_out, rom_2_data;
  wire [4:0] adder_1_out, and_1_out, controlled_buffer_3_out, controlled_buffer_5_out,
       controlled_buffer_16_out, counter_1_q, nand_1_out, not_4_out, or_2_out, register_1_q, rom_1_data,
       xor_1_out, xor_2_out;
  wire [4:4] demultiplexer_1_out8;

  Counter #(.width(5), .max('h1f), .trigger("falling")) counter_1 (
    .load(demultiplexer_1_out13), .D(controlled_buffer_3_out), .count(not_1_out), .Q(counter_1_q),
    .clk(pull_resistor_1_node), .clr(RESET_out));  // open: carry
  not not_1 (not_1_out, demultiplexer_1_out13);
  Pull_Resistor pull_resistor_1 (.node(pull_resistor_1_node));
  assign pull_resistor_1_node = not_3_out ? clock_1_out : 1'bz;  // Controlled_Buffer controlled_buffer_1
  Button GO (.out(GO_out));
  Clock clock_1 (.out(clock_1_out));
  Button RESET (.out(RESET_out));
  Pull_Resistor pull_resistor_2 (.node(pull_resistor_2_node));
  assign pull_resistor_2_node = not_3_out ? clock_1_out : 1'bz;  // Controlled_Buffer controlled_buffer_2
  assign controlled_buffer_3_out = not_2_out ? rom_1_data : 5'bz;  // Controlled_Buffer controlled_buffer_3
  ROM #(.addrWidth(5), .dataWidth(5)) rom_1 (.addr(counter_1_q), .data(rom_1_data));  // open: sel
  Demultiplexer #(.select(4), .disabled(0), .enable("false")) demultiplexer_1 (
    .out1(demultiplexer_1_out1), .out2(demultiplexer_1_out2), .out3(demultiplexer_1_out3),
    .out4(demultiplexer_1_out4), .out5(demultiplexer_1_out5), .out6(demultiplexer_1_out6),
    .out7(demultiplexer_1_out7), .out8(demultiplexer_1_out8[4]), .out9(demultiplexer_1_out9),
    .out10(demultiplexer_1_out10), .out11(demultiplexer_1_out11), .out12(demultiplexer_1_out12),
    .out13(demultiplexer_1_out13), .out14(demultiplexer_1_out14), .out15(demultiplexer_1_out15), .in(1'b1),
    .sel(controlled_buffer_4_out));  // open: out0
  ROM #(.addrWidth(5), .dataWidth(4)) rom_2 (.addr(counter_1_q), .data(rom_2_data));  // open: sel
  assign controlled_buffer_4_out = not_2_out ? rom_2_data : 4'bz;  // Controlled_Buffer controlled_buffer_4
  Pull_Resistor pull_resistor_3 (.node(controlled_buffer_3_out));
  Pull_Resistor pull_resistor_4 (.node(controlled_buffer_4_out));
  Register #(.width(5), .trigger("falling")) register_1 (
    .D(controlled_buffer_5_out), .Q(register_1_q), .clk(pull_resistor_2_node), .clr(RESET_out));  // open: en
  assign nand_1_out = ~(register_1_q & controlled_buffer_3_out);  // NAND_Gate nand_1, 5 bits wide
  assign controlled_buffer_5_out = demultiplexer_1_out1 ? nand_1_out : 5'bz;  // Controlled_Buffer controlled_buffer_5
  not not_2 (not_2_out, SKIP);
  not not_3 (not_3_out, HALT);
  assign and_1_out = register_1_q & controlled_buffer_3_out;  // AND_Gate and_1, 5 bits wide
  assign controlled_buffer_5_out = demultiplexer_1_out2 ? and_1_out : 5'bz;  // Controlled_Buffer controlled_buffer_6
  or or_1 (or_1_out, RESET_out, GO_out);
  assign xor_1_out = register_1_q ^ controlled_buffer_3_out;  // XOR_Gate xor_1, 5 bits wide
  assign controlled_buffer_5_out = demultiplexer_1_out3 ? xor_1_out : 5'bz;  // Controlled_Buffer controlled_buffer_7
  assign controlled_buffer_5_out = demultiplexer_1_out14 ? {register_1_q[0], register_1_q[4:1]} : 5'bz;  // Controlled_Buffer controlled_buffer_8
  assign or_2_out = register_1_q | controlled_buffer_3_out;  // OR_Gate or_2, 5 bits wide
  assign controlled_buffer_5_out = demultiplexer_1_out4 ? or_2_out : 5'bz;  // Controlled_Buffer controlled_buffer_9
  J_K_Flip_Flop j_k_ff_1 (
    .J(demultiplexer_1_out15), .clk(pull_resistor_2_node), .K(1'b0), .Q(HALT), .reset(or_1_out));  // open: Qn, preset, en
  assign controlled_buffer_5_out = demultiplexer_1_out5 ? controlled_buffer_3_out : 5'bz;  // Controlled_Buffer controlled_buffer_10
  assign not_4_out = ~register_1_q;  // NOT_Gate not_4, 5 bits wide
  assign controlled_buffer_5_out = demultiplexer_1_out11 ? not_4_out : 5'bz;  // Controlled_Buffer controlled_buffer_11
  assign xor_2_out = controlled_buffer_3_out ^ {5{demultiplexer_1_out8[4]}};  // XOR_Gate xor_2, 5 bits wide
  assign controlled_buffer_5_out = demultiplexer_1_out7 ? adder_1_out : 5'bz;  // Controlled_Buffer controlled_buffer_12
  Shift_Register #(.length(1)) shift_register_1 (
    .in(1'b0), .clk(pull_resistor_2_node), .out(SKIP), .load(or_3_out), .clr(RESET_out), .d0(1'b1));  // open: shift, q0
  Adder #(.width(5)) adder_1 (
    .a(register_1_q), .b(xor_2_out), .out(adder_1_out), .cin(demultiplexer_1_out8[4]));  // open: cout
  assign controlled_buffer_5_out = demultiplexer_1_out8[4] ? adder_1_out : 5'bz;  // Controlled_Buffer controlled_buffer_13
  Comparator #(.width(5)) comparator_1 (
    .a(controlled_buffer_3_out), .b(register_1_q), .eq(comparator_1_eq));  // open: gt, lt
  assign controlled_buffer_14_out = demultiplexer_1_out6 ? comparator_1_eq : 1'bz;  // Controlled_Buffer controlled_buffer_14
  Pull_Resistor pull_resistor_5 (.node(controlled_buffer_14_out));
  not not_5 (not_5_out, comparator_1_eq);
  Pull_Resistor pull_resistor_6 (.node(pull_resistor_6_node));
  assign pull_resistor_6_node = demultiplexer_1_out12 ? not_5_out : 1'bz;  // Controlled_Buffer controlled_buffer_15
  or or_3 (or_3_out, controlled_buffer_14_out, pull_resistor_6_node);
  or or_4 (or_4_out, demultiplexer_1_out9, demultiplexer_1_out10);
  assign controlled_buffer_16_out = demultiplexer_1_out9 ? register_1_q : 5'bz;  // Controlled_Buffer controlled_buffer_16
  RAM #(.addrWidth(5), .dataWidth(5)) ram_1 (
    .addr(controlled_buffer_3_out), .data(controlled_buffer_16_out), .sel(or_4_out),
    .clk(pull_resistor_2_node), .ld(demultiplexer_1_out10), .clr(RESET_out));
  assign controlled_buffer_5_out = demultiplexer_1_out10 ? controlled_buffer_16_out : 5'bz;  // Controlled_Buffer controlled_buffer_17

  // Notes on the sheet:
  //   contents of rom_1 (hex, n*v repeats v):
  //   0 0 1 5 0 2
  //   contents of rom_2 (hex, n*v repeats v):
  //   6 5 8 c f d
endmodule
